# Fritzing sketch PET project schematic (saved by Fritzing 0.9.9b)
breadboards: 1

parts:
  M1 = DC Motor
  Part1 = Arduino Uno (Rev3)
  R1 = Photocell (LDR) [package=THT]
  R2 = Photocell (LDR) [package=THT]
  R3 = Photocell (LDR) [package=THT]
  VCC1 = Battery
  M2 = DC Motor
  J1 = Basic Servo
  EDGY_motor_control1 = EDGY  # not connected
  LED1 = LED - 5mm [color="Red (633nm)" current=0.030 package="5 mm [THT]"]
  LED2 = LED - 5mm [color="Red (633nm)" current=0.030 package="5 mm [THT]"]
  LED3 = LED - 5mm [color="Red (633nm)" current=0.030 package="5 mm [THT]"]
  R4 = Resistor [tolerance=±5% power=0.25 resistance=220 package=THT]
  R5 = Resistor [tolerance=±5% power=0.25 resistance=220 package=THT]
  R6 = Resistor [tolerance=±5% power=0.25 resistance=220 package=THT]

nets:
  N1: M1.pin_1, VCC1.+, M2.pin_1, J1.vcc
  N2: M1.pin_2, VCC1.-, M2.pin_2, J1.gnd
  N3: Part1.A0, Part1.A1, Part1.A2, Part1.GND, R1.pin_1, R2.pin_1, R3.pin_1, R4.Pin_1, R5.Pin_1, R6.Pin_1
  N4: Part1.D8, J1.pulse
  N5: Part1.5V, R1.pin_0, R2.pin_0, R3.pin_0, LED1.anode, LED2.anode, LED3.anode
  N6: LED1.cathode, R5.Pin_0
  N7: LED2.cathode, R4.Pin_0
  N8: LED3.cathode, R6.Pin_0
